# Fritzing sketch StopWatchSender (saved by Fritzing 0.9.3b)
circuit board: 5.64444cm x 8.46667cm
breadboards: 1

parts:
  3_3V_-_8MHz = Arduino Pro Mini v13
  Stop = Pushbutton [package=THT]
  Start0 = Pushbutton [package=THT]
  Start1 = Pushbutton [package=THT]
  Start2 = Pushbutton [package=THT]
  Start3 = Pushbutton [package=THT]
  J1 = Piezo Speaker
  V1 = DC Power [voltage=5]
  nRF24L01+_PA_LNA = NRF24L01+ Breakout Board
  C1 = Electrolytic Capacitor [capacitance=47µF voltage=10V package="100 mil [THT, electrolytic]"]

nets:
  VCC: 3_3V_-_8MHz.VCC, nRF24L01+_PA_LNA.VCC, C1.+
  GND: 3_3V_-_8MHz.GND, Stop.leg1, Start0.leg1, Start1.leg1, Start2.leg1, Start3.leg1, J1.pin1, V1.V-, nRF24L01+_PA_LNA.GND, C1.-
  N1: 3_3V_-_8MHz.RAW, V1.V+
  N2: 3_3V_-_8MHz.A0, J1.pin2
  N3: 3_3V_-_8MHz.D13/SCK, nRF24L01+_PA_LNA.SCK
  N4: 3_3V_-_8MHz.D12/MISO, nRF24L01+_PA_LNA.MISO
  N5: 3_3V_-_8MHz.D11_PWM/MOSI, nRF24L01+_PA_LNA.MOSI
  N6: 3_3V_-_8MHz.D10_PWM/SS, nRF24L01+_PA_LNA.CS
  N7: 3_3V_-_8MHz.D9_PWM, nRF24L01+_PA_LNA.CE
  N8: 3_3V_-_8MHz.D7, Start3.leg0
  N9: 3_3V_-_8MHz.D6_PWM, Start2.leg0
  N10: 3_3V_-_8MHz.D5_PWM, Start1.leg0
  N11: 3_3V_-_8MHz.D4, Start0.leg0
  N12: 3_3V_-_8MHz.D3_PWM, Stop.leg0
  N13: 3_3V_-_8MHz.D2, nRF24L01+_PA_LNA.IRQ

notes:
  StopWatchSender
